// Logisim project basic-computer.circ as structural Verilog: 3 circuits, main circuit main
module main (
  input  [15:0] in_1,
  output [2:0] out_2
);

  wire CLK, CLR_SC, d_ff_1_q, INC_PC, LD_AC, LD_AR, LD_DR, LD_IR, LD_M, LD_PC, LD_TR, WR_M;
  wire [2:0] ALU_C;
  wire [3:0] counter_1_q;
  wire [6:0] AR_q, bit_extender_1_out, bit_extender_2_out, PC_q;
  wire [15:0] AC, AC_IN, bit_extender_3_out, bit_extender_4_out, DR, IR, multiplexer_1_out, ram_1_data, TR_q;

  Bit_Extender #(.in_width(16), .out_width(7)) bit_extender_1 (.in(multiplexer_1_out), .out(bit_extender_1_out));
  Bit_Extender #(.in_width(16), .out_width(7)) bit_extender_2 (.in(multiplexer_1_out), .out(bit_extender_2_out));
  D_Flip_Flop d_ff_1 (.clk(CLK), .D(CLR_SC), .Q(d_ff_1_q));  // open: Qn, preset, en, reset
  Register #(.width(16)) u_AC (.D(AC_IN), .en(LD_AC), .Q(AC), .clk(CLK));  // open: clr
  Register #(.width(16)) TR (.D(multiplexer_1_out), .en(LD_TR), .Q(TR_q), .clk(CLK));  // open: clr
  Counter #(.width(4), .max('hf)) counter_1 (
    .Q(counter_1_q), .clk(CLK), .clr(d_ff_1_q));  // open: load, D, count, carry
  Register #(.width(7)) AR (.D(bit_extender_1_out), .en(LD_AR), .Q(AR_q), .clk(CLK));  // open: clr
  Register #(.width(16)) u_DR (.D(multiplexer_1_out), .en(LD_DR), .Q(DR), .clk(CLK));  // open: clr
  CU cu_1 (
    .IR(IR), .SC(counter_1_q), .DR(DR), .C2(ALU_C[2]), .CLR_SC(CLR_SC), .LD_TR(LD_TR), .C1(ALU_C[1]),
    .LD_PC(LD_PC), .C0(ALU_C[0]), .LD_DR(LD_DR), .LD_AC(LD_AC), .WR_M(WR_M), .LD_M(LD_M), .LD_IR(LD_IR),
    .INC_PC(INC_PC), .ZLD_AR(LD_AR), .S1_B(out_2[1]), .S2_B(out_2[2]), .S0_B(out_2[0]));
  Counter #(.width(7), .max('h7f)) PC (
    .load(LD_PC), .D(bit_extender_2_out), .count(INC_PC), .Q(PC_q), .clk(CLK));  // open: carry, clr
  Register #(.width(16)) u_IR (.D(multiplexer_1_out), .en(LD_IR), .Q(IR), .clk(CLK));  // open: clr
  assign bit_extender_3_out = {{9{1'b0}}, AR_q};  // Bit_Extender bit_extender_3
  assign bit_extender_4_out = {{9{1'b0}}, PC_q};  // Bit_Extender bit_extender_4
  RAM #(.addrWidth(7), .dataWidth(16), .bus("separate")) ram_1 (
    .addr(AR_q), .din(multiplexer_1_out), .data(ram_1_data), .str(LD_M), .clk(CLK), .ld(WR_M));  // open: sel, clr
  Clock u_Clk (.out(CLK));
  Multiplexer #(.select(3), .width(16), .enable("false")) multiplexer_1 (
    .in0(ram_1_data), .in1(bit_extender_3_out), .in2(bit_extender_4_out), .in3(AC), .in4(DR), .in5(TR_q),
    .in6(in_1), .in7(IR), .out(multiplexer_1_out), .sel(out_2));
  ALU ALU (.A(DR), .B(AC), .OUT(AC_IN), .Ctrl(ALU_C));

  // Other names for the same wires on the sheet: C0 = ALU_C[0]; C1 = ALU_C[1]; C2 = ALU_C[2]; BUS_C[2:0] = out_2;
  //   S0 = out_2[0]; S1 = out_2[1]; S2 = out_2[2]
endmodule

module ALU (
  input  [15:0] A,
  input  [15:0] B,
  input  [2:0] Ctrl,
  output [15:0] OUT
);

  wire [15:0] adder_1_out, adder_2_out, divider_1_out, multiplier_1_out, subtractor_1_out, xor_1_out;

  Adder #(.width(16)) adder_1 (.a(A), .b({16{1'b0}}), .out(adder_1_out), .cin(1'b1));  // open: cout
  Multiplier #(.width(16)) multiplier_1 (.a(A), .b(B), .out(multiplier_1_out));  // open: cin, cout
  Subtractor #(.width(16)) subtractor_1 (.a(A), .b(B), .out(subtractor_1_out));  // open: bin, bout
  Divider #(.width(16)) divider_1 (.a(A), .b(B), .out(divider_1_out));  // open: upper, rem
  Adder #(.width(16)) adder_2 (.a(A), .b(B), .out(adder_2_out));  // open: cin, cout
  assign xor_1_out = A ^ B;  // XOR_Gate xor_1, 16 bits wide
  Multiplexer #(.select(3), .width(16), .disabled(0), .enable("false")) multiplexer_1 (
    .in1(A), .in2(adder_1_out), .in3(multiplier_1_out), .in4(subtractor_1_out), .in5(divider_1_out),
    .in6(adder_2_out), .in7(xor_1_out), .out(OUT), .sel(Ctrl));  // open: in0
endmodule

module CU (
  input  [15:0] IR,
  input  [3:0] SC,
  input  [15:0] DR,
  output C2,
  output CLR_SC,
  output LD_TR,
  output C1,
  output LD_PC,
  output C0,
  output LD_DR,
  output LD_AC,
  output WR_M,
  output LD_M,
  output LD_IR,
  output INC_PC,
  output ZLD_AR,
  output S1_B,
  output S2_B,
  output S0_B
);

  wire and_7_out, and_13_out, and_14_out, and_15_out, and_20_out, D0, D0_T4, D0_T6, D0_T7, D1, D1_T4, D1_T5,
       D2, D2_T4, D2_T5, D3, D3_T4, D4, D5, D5_T5, D6, D6_T4, D6_T5, D6_T6, D6_T7, D7, nor_1_out, or_4_out,
       or_5_out, or_6_out, or_8_out, or_14_out, T0, T2, T3, T4, T5, T6, T7, T8, T9, T10, T11, T12, T13, T14,
       T15;

  Decoder #(.select(4), .enable("false")) decoder_1 (
    .out0(T0), .out1(LD_IR), .out2(T2), .out3(T3), .out4(T4), .out5(T5), .out6(T6), .out7(T7), .out8(T8),
    .out9(T9), .out10(T10), .out11(T11), .out12(T12), .out13(T13), .out14(T14), .out15(T15), .sel(SC));
  or or_1 (ZLD_AR, T2, T0);
  and and_1 (D1_T4, D1, T4);
  and and_2 (D2_T4, D2, T4);
  Decoder #(.select(3), .enable("false")) decoder_2 (
    .out0(D0), .out1(D1), .out2(D2), .out3(D3), .out4(D4), .out5(D5), .out6(D6), .out7(D7), .sel(IR[14:12]));
  and and_3 (LD_PC, D4, T4);
  and and_4 (D2_T5, D2, T5);
  nor nor_1 (nor_1_out, DR[0], DR[1], DR[2], DR[3], DR[4], DR[5], DR[6], DR[7], DR[9], DR[10], DR[11], DR[12], DR[13], DR[14], DR[15], DR[8]);
  and and_5 (D6_T7, D6, T7);
  and and_6 (D0_T7, D0, T7);
  and and_7 (and_7_out, D6_T7, nor_1_out);
  or or_2 (INC_PC, and_7_out, LD_IR);
  and and_8 (D3_T4, D3, T4);
  and and_9 (D1_T5, D1, T5);
  and and_10 (D5_T5, D5, T5);
  and and_11 (LD_TR, D0, T5);
  or or_3 (CLR_SC, LD_PC, D6_T7, D0_T7, D3_T4, D1_T5, D2_T5, D5_T5);
  or or_4 (or_4_out, D5, or_5_out);
  or or_5 (or_5_out, D0, D1, D2, D6);
  or or_6 (or_6_out, D5, D1, D0, D2, D6);
  or or_7 (S1_B, D6_T6, T0, LD_TR, T2, D3_T4);
  or or_8 (or_8_out, D6_T6, LD_TR, T2, D3_T4, LD_PC);
  or or_9 (S0_B, or_8_out, D0_T6);
  and and_12 (D0_T4, D0, T4);
  and and_13 (and_13_out, T4, or_4_out);
  and and_14 (and_14_out, T6, D0);
  and and_15 (and_15_out, or_6_out, T5);
  or or_10 (LD_AC, D0_T7, and_15_out);
  or or_11 (LD_M, D6_T7, D3_T4);
  and and_16 (D6_T6, D6, T6);
  and and_17 (D0_T6, D0, T6);
  or or_12 (LD_DR, and_13_out, D6_T6, and_14_out);
  or or_13 (S2_B, D6_T7, T2, D0_T6);
  and and_18 (D6_T4, D6, T4);
  and and_19 (D6_T5, D6, T5);
  or or_14 (or_14_out, D1_T4, D0_T4, LD_IR, D6_T4, D2_T4);
  or or_15 (C2, D0_T7, D1_T5);
  or or_16 (C1, D6_T5, D5_T5, D1_T5);
  or or_17 (C0, D2_T5, D0_T7, LD_TR, D5_T5);
  and and_20 (and_20_out, D5, T4);
  or or_18 (WR_M, or_14_out, and_20_out);

  // Other names for the same wires on the sheet: D0_T5 = LD_TR; D4_T4 = LD_PC; S0 = S0_B; S1 = S1_B; S2 = S2_B;
  //   STR_M = LD_M; T1 = LD_IR
endmodule
