// Logisim project milestone1-datapath.circ as structural Verilog: 2 circuits, main circuit main
module main (
  input  Write,
  input  Read,
  input  Load_AR,
  input  Load_PC,
  input  [15:0] in_5,
  input  Load_AC,
  input  Load_DR,
  input  [2:0] S2_S1_S0,
  input  Load_TR,
  input  Load_IR,
  input  [2:0] C2_C1_C0
);

  wire Clk_out;
  wire [6:0] AR_q, bit_extender_1_out, bit_extender_2_out, PC_q;
  wire [15:0] AC_q, ALU_out, bit_extender_3_out, bit_extender_4_out, DR_q, IR_q, multiplexer_1_out,
       ram_1_data, TR_q;

  Bit_Extender #(.in_width(16), .out_width(7)) bit_extender_1 (.in(multiplexer_1_out), .out(bit_extender_1_out));
  Bit_Extender #(.in_width(16), .out_width(7)) bit_extender_2 (.in(multiplexer_1_out), .out(bit_extender_2_out));
  Clock Clk (.out(Clk_out));
  Register #(.width(16)) TR (.D(multiplexer_1_out), .en(Load_TR), .Q(TR_q), .clk(Clk_out));  // open: clr
  Register #(.width(7)) AR (.D(bit_extender_1_out), .en(Load_AR), .Q(AR_q), .clk(Clk_out));  // open: clr
  Register #(.width(7)) PC (.D(bit_extender_2_out), .en(Load_PC), .Q(PC_q), .clk(Clk_out));  // open: clr
  Register #(.width(16)) AC (.D(ALU_out), .en(Load_AC), .Q(AC_q), .clk(Clk_out));  // open: clr
  Register #(.width(16)) DR (.D(multiplexer_1_out), .en(Load_DR), .Q(DR_q), .clk(Clk_out));  // open: clr
  Register #(.width(16)) IR (.D(multiplexer_1_out), .en(Load_IR), .Q(IR_q), .clk(Clk_out));  // open: clr
  RAM #(.addrWidth(7), .dataWidth(16), .bus("separate")) ram_1 (
    .addr(AR_q), .din(multiplexer_1_out), .data(ram_1_data), .str(Write), .clk(Clk_out), .ld(Read));  // open: sel, clr
  assign bit_extender_3_out = {{9{1'b0}}, AR_q};  // Bit_Extender bit_extender_3
  assign bit_extender_4_out = {{9{1'b0}}, PC_q};  // Bit_Extender bit_extender_4
  ALU ALU (.A(DR_q), .B(AC_q), .c2_c1_c0(C2_C1_C0), .OUT(ALU_out));
  Multiplexer #(.select(3), .width(16), .enable("false")) multiplexer_1 (
    .in0(ram_1_data), .in1(bit_extender_3_out), .in2(bit_extender_4_out), .in3(AC_q), .in4(DR_q), .in5(TR_q),
    .in6(in_5), .in7(IR_q), .out(multiplexer_1_out), .sel(S2_S1_S0));
endmodule

module ALU (
  input  [15:0] A,
  input  [15:0] B,
  input  [2:0] c2_c1_c0,
  output [15:0] OUT
);

  wire [15:0] adder_1_out, adder_2_out, divider_1_out, multiplier_1_out, subtractor_1_out, xor_1_out;

  Adder #(.width(16)) adder_1 (.a(A), .b({16{1'b0}}), .out(adder_1_out), .cin(1'b1));  // open: cout
  Multiplier #(.width(16)) multiplier_1 (.a(A), .b(B), .out(multiplier_1_out));  // open: cin, cout
  Subtractor #(.width(16)) subtractor_1 (.a(A), .b(B), .out(subtractor_1_out));  // open: bin, bout
  Divider #(.width(16)) divider_1 (.a(A), .b(B), .out(divider_1_out));  // open: upper, rem
  Adder #(.width(16)) adder_2 (.a(A), .b(B), .out(adder_2_out));  // open: cin, cout
  assign xor_1_out = A ^ B;  // XOR_Gate xor_1, 16 bits wide
  Multiplexer #(.select(3), .width(16), .disabled(0), .enable("false")) multiplexer_1 (
    .in1(A), .in2(adder_1_out), .in3(multiplier_1_out), .in4(subtractor_1_out), .in5(divider_1_out),
    .in6(adder_2_out), .in7(xor_1_out), .out(OUT), .sel(c2_c1_c0));  // open: in0
endmodule
